// Logisim project c121.circ as structural Verilog: 8 circuits, main circuit main
module main (
);

  wire button_1_out, clock_1_out, cpu_1_wr_en, decoder_1_out0, decoder_1_out1, decoder_1_out2,
       decoder_2_out0, decoder_2_out1, decoder_2_out2, decoder_2_out3, decoder_2_out4, decoder_2_out5,
       decoder_2_out6, decoder_2_out7, not_1_out;
  wire [3:0] cpu_1_a;
  wire [11:0] button_13_out, controlled_buffer_1_out, cpu_1_do, register_1_q, register_2_q, register_3_q,
       register_4_q, register_5_q, register_6_q, register_7_q;
  wire [11:4] cpu_1_a_2;

  Hex_Digit_Display hex_digit_display_1 (.value(cpu_1_a_2[11:8]));  // open: dp
  Clock clock_1 (.out(clock_1_out));
  Button button_1 (.out(button_1_out));
  Hex_Digit_Display hex_digit_display_2 (.value(cpu_1_a));  // open: dp
  Hex_Digit_Display hex_digit_display_3 (.value(cpu_1_a_2[7:4]));  // open: dp
  Decoder #(.select(3)) decoder_1 (
    .out0(decoder_1_out0), .out1(decoder_1_out1), .out2(decoder_1_out2), .sel(cpu_1_a_2[11:9]), .en(1'b1));  // open: out3, out4, out5, out6, out7
  CPU cpu_1 (
    .CLK(clock_1_out), .RST(button_1_out), .A({cpu_1_a_2, cpu_1_a}), .DO(cpu_1_do),
    .DI(controlled_buffer_1_out), .WR_EN(cpu_1_wr_en));  // open: RD_EN
  assign controlled_buffer_1_out = cpu_1_wr_en ? cpu_1_do : 12'bz;  // Controlled_Buffer controlled_buffer_1
  Hex_Digit_Display hex_digit_display_4 (.value(controlled_buffer_1_out[11:8]));  // open: dp
  not not_1 (not_1_out, cpu_1_wr_en);
  Hex_Digit_Display hex_digit_display_5 (.value(controlled_buffer_1_out[7:4]));  // open: dp
  Hex_Digit_Display hex_digit_display_6 (.value(controlled_buffer_1_out[3:0]));  // open: dp
  Decoder #(.select(3), .disabled(0)) decoder_2 (
    .out0(decoder_2_out0), .out1(decoder_2_out1), .out2(decoder_2_out2), .out3(decoder_2_out3),
    .out4(decoder_2_out4), .out5(decoder_2_out5), .out6(decoder_2_out6), .out7(decoder_2_out7),
    .sel(cpu_1_a[2:0]), .en(decoder_1_out2));
  ROM #(.addrWidth(9), .dataWidth(12)) rom_1 (
    .addr({cpu_1_a_2[8:4], cpu_1_a}), .data(controlled_buffer_1_out), .sel(decoder_1_out0));
  RAM #(.addrWidth(9), .dataWidth(12)) ram_1 (
    .addr({cpu_1_a_2[8:4], cpu_1_a}), .data(controlled_buffer_1_out), .sel(decoder_1_out1),
    .clk(clock_1_out), .ld(not_1_out));  // open: clr
  assign controlled_buffer_1_out = decoder_2_out7 ? button_13_out : 12'bz;  // Controlled_Buffer controlled_buffer_2
  Register #(.width(12)) register_1 (
    .D(controlled_buffer_1_out), .en(decoder_2_out0), .Q(register_1_q), .clk(clock_1_out));  // open: clr
  Register #(.width(12)) register_2 (
    .D(controlled_buffer_1_out), .en(decoder_2_out2), .Q(register_2_q), .clk(clock_1_out));  // open: clr
  Register #(.width(12)) register_3 (
    .D(controlled_buffer_1_out), .en(decoder_2_out4), .Q(register_3_q), .clk(clock_1_out));  // open: clr
  Register #(.width(12)) register_4 (
    .D(controlled_buffer_1_out), .Q(register_4_q), .clk(clock_1_out));  // open: en, clr
  DotMatrix #(.inputtype("row"), .matrixcols(12)) dotmatrix_1 (
    .row0(register_1_q), .row1(register_5_q), .row2(register_2_q), .row3(register_6_q), .row4(register_3_q),
    .row5(register_7_q), .row6(register_4_q));
  Register #(.width(12)) register_5 (
    .D(controlled_buffer_1_out), .en(decoder_2_out1), .Q(register_5_q), .clk(clock_1_out));  // open: clr
  Register #(.width(12)) register_6 (
    .D(controlled_buffer_1_out), .en(decoder_2_out3), .Q(register_6_q), .clk(clock_1_out));  // open: clr
  Register #(.width(12)) register_7 (
    .D(controlled_buffer_1_out), .en(decoder_2_out5), .Q(register_7_q), .clk(clock_1_out));  // open: clr
  Button button_2 (.out(button_13_out[10]));
  Button button_3 (.out(button_13_out[8]));
  Button button_4 (.out(button_13_out[11]));
  Button button_5 (.out(button_13_out[9]));
  Button button_6 (.out(button_13_out[7]));
  Button button_7 (.out(button_13_out[6]));
  Button button_8 (.out(button_13_out[5]));
  Button button_9 (.out(button_13_out[4]));
  Button button_10 (.out(button_13_out[3]));
  Button button_11 (.out(button_13_out[2]));
  Button button_12 (.out(button_13_out[1]));
  Button button_13 (.out(button_13_out[0]));

  // Notes on the sheet:
  //   contents of rom_1 (hex, n*v repeats v):
  //   801 902 a03 b04
endmodule

module CPU (
  input  CLK,
  input  RST,
  input  [11:0] DI,
  output [11:0] A,
  output [11:0] DO,
  output WR_EN,
  output RD_EN
);

  wire and_1_out, clockgen_1_p1, clockgen_1_p2, clockgen_1_p3, instructioncontrol_1_ir0_valid,
       pipest1_1_en_a, pipest1_1_ins_strobe, pipest1_1_out_ready, undriven;
  wire [1:0] decode_t1_1_srcmode;
  wire [3:0] decode_t1_1_dstreg, decode_t1_1_srcreg, pipest1_1_out_dstreg, pipest1_1_sel_a;
  wire [4:0] decode_t1_1_op, pipest1_1_out_opcode;
  wire [11:0] decode_t1_1_immwd, instructioncontrol_1_ir0, pipest1_1_out_data, regfile_1_ip, regfile_1_op_a;

  assign DO = RD_EN ? DI : 12'bz;  // Controlled_Buffer controlled_buffer_1
  clockgen clockgen_1 (.CLK(CLK), .P1(clockgen_1_p1), .P2(clockgen_1_p2), .P3(clockgen_1_p3));
  InstructionControl instructioncontrol_1 (
    .IFETCH(RD_EN), .IR0_VALID(instructioncontrol_1_ir0_valid), .IR0_CONSUMED(pipest1_1_ins_strobe),
    .IR0(instructioncontrol_1_ir0), .CLK_P1(clockgen_1_p1), .CLK_P2(clockgen_1_p2), .CLK_P3(clockgen_1_p3),
    .D_IN(DO), .WAIT(1'b0));  // open: IQRESET, IR1_VALID, IR1_CONSUMED, IR1
  decode_t1 decode_t1_1 (
    .INSTR(instructioncontrol_1_ir0), .OP(decode_t1_1_op), .DSTREG(decode_t1_1_dstreg),
    .SRCREG(decode_t1_1_srcreg), .SRCMODE(decode_t1_1_srcmode), .IMMWD(decode_t1_1_immwd));
  PipeSt1 pipest1_1 (
    .A(regfile_1_op_a), .INS_STROBE(pipest1_1_ins_strobe), .OUT_DATA(pipest1_1_out_data),
    .OUT_OPCODE(pipest1_1_out_opcode), .OUT_DSTREG(pipest1_1_out_dstreg), .PS2_ACK(and_1_out),
    .EN_A(pipest1_1_en_a), .SEL_A(pipest1_1_sel_a), .OPCODE(decode_t1_1_op), .DSTREG(decode_t1_1_dstreg),
    .SRCREG(decode_t1_1_srcreg), .SRCMODE(decode_t1_1_srcmode), .IMMWD(decode_t1_1_immwd),
    .IR_VALID(instructioncontrol_1_ir0_valid), .OUT_READY(pipest1_1_out_ready));  // open: CLK
  and and_1 (and_1_out, pipest1_1_out_ready, ~undriven);  // AND_Gate
  assign A = RD_EN ? regfile_1_ip : 12'bz;  // Controlled_Buffer controlled_buffer_2
  REGFILE regfile_1 (
    .EN_A(pipest1_1_en_a), .SEL_A(pipest1_1_sel_a), .IP_INC(RD_EN), .OP_A(regfile_1_op_a), .IP(regfile_1_ip));  // open: EN_B, SEL_B, CLK, D, SEL_LD, EN_LD, OP_B

  assign WR_EN = 1'b0;

  // Other names for the same wires on the sheet: IFETCH = RD_EN
endmodule

// DecT1
module decode_t1 (
  input  [11:0] INSTR,
  output [4:0] OP,
  output [3:0] DSTREG,
  output [3:0] SRCREG,
  output [1:0] SRCMODE,
  output [11:0] IMMWD
);

  wire and_1_out;
  wire [1:0] bit_extender_1_out;
  wire [11:0] bit_extender_2_out;

  and and_1 (and_1_out, INSTR[9], INSTR[5]);
  assign bit_extender_1_out = {{1{1'b0}}, INSTR[10]};  // Bit_Extender bit_extender_1
  assign bit_extender_2_out = {{6{and_1_out}}, INSTR[5:0]};  // Bit_Extender bit_extender_2
  assign OP = INSTR[11] ? 5'b00001 : 5'bz;  // Controlled_Buffer controlled_buffer_1
  assign DSTREG = INSTR[11] ? INSTR[9:6] : 4'bz;  // Controlled_Buffer controlled_buffer_2
  assign SRCREG = INSTR[11] ? 4'b1111 : 4'bz;  // Controlled_Buffer controlled_buffer_3
  assign SRCMODE = INSTR[11] ? bit_extender_1_out : 2'bz;  // Controlled_Buffer controlled_buffer_4
  assign IMMWD = INSTR[11] ? bit_extender_2_out : 12'bz;  // Controlled_Buffer controlled_buffer_5

  // Notes on the sheet:
  //   Decoder for instruction format 1:
  //   Instruction format is: 1brrrrnnnnnnn, where:
  //   b = 0 for direct operand, 1 for PC-relative address
  //   rrrr = target register
  //   nnnnnn = immediate operand / offset
  //   Only instruction implemented is MOV (1)
  //   Immediate operand is zero-extended when destination is reg 0-7,
  //   or sign-extended when destination is reg 8-15
endmodule

// RegFile
module REGFILE (
  input  EN_A,
  input  [3:0] SEL_A,
  input  EN_B,
  input  [3:0] SEL_B,
  input  CLK,
  input  [11:0] D,
  input  [3:0] SEL_LD,
  input  EN_LD,
  input  IP_INC,
  output [11:0] OP_A,
  output [11:0] OP_B,
  output [11:0] IP
);

  wire decoder_1_out0, decoder_1_out1, decoder_1_out2, decoder_1_out3, decoder_1_out4, decoder_1_out5,
       decoder_1_out6, decoder_1_out7, decoder_1_out8, decoder_1_out9, decoder_1_out10, decoder_1_out11,
       decoder_1_out12, decoder_1_out13, decoder_1_out14, decoder_1_out15, or_1_out, or_2_out,
       pull_resistor_1_node;
  wire [11:0] adder_1_out, multiplexer_3_out, multiplexer_4_out, register_1_q, register_2_q, register_3_q,
       register_4_q, register_5_q, register_6_q, register_7_q, register_8_q, register_9_q, register_10_q,
       register_11_q, register_12_q, register_13_q, register_14_q, register_16_q;

  Decoder #(.select(4), .disabled(0)) decoder_1 (
    .out0(decoder_1_out0), .out1(decoder_1_out1), .out2(decoder_1_out2), .out3(decoder_1_out3),
    .out4(decoder_1_out4), .out5(decoder_1_out5), .out6(decoder_1_out6), .out7(decoder_1_out7),
    .out8(decoder_1_out8), .out9(decoder_1_out9), .out10(decoder_1_out10), .out11(decoder_1_out11),
    .out12(decoder_1_out12), .out13(decoder_1_out13), .out14(decoder_1_out14), .out15(decoder_1_out15),
    .sel(SEL_LD), .en(EN_LD));
  Register #(.width(12)) register_1 (.D(D), .en(decoder_1_out0), .Q(register_1_q), .clk(CLK));  // open: clr
  Register #(.width(12)) register_2 (.D(D), .en(decoder_1_out1), .Q(register_2_q), .clk(CLK));  // open: clr
  Register #(.width(12)) register_3 (.D(D), .en(decoder_1_out2), .Q(register_3_q), .clk(CLK));  // open: clr
  Register #(.width(12)) register_4 (.D(D), .en(decoder_1_out3), .Q(register_4_q), .clk(CLK));  // open: clr
  Multiplexer #(.select(4), .width(12)) multiplexer_1 (
    .in0(register_1_q), .in1(register_2_q), .in2(register_3_q), .in3(register_4_q), .in4(register_5_q),
    .in5(register_6_q), .in6(register_7_q), .in7(register_8_q), .in8(register_9_q), .in9(register_10_q),
    .in10(register_11_q), .in11(register_12_q), .in12(register_13_q), .in13(register_14_q),
    .in14(register_16_q), .in15(IP), .out(OP_A), .sel(SEL_A), .en(EN_A));
  Register #(.width(12)) register_5 (.D(D), .en(decoder_1_out4), .Q(register_5_q), .clk(CLK));  // open: clr
  Register #(.width(12)) register_6 (.D(D), .en(decoder_1_out5), .Q(register_6_q), .clk(CLK));  // open: clr
  Register #(.width(12)) register_7 (.D(D), .en(decoder_1_out6), .Q(register_7_q), .clk(CLK));  // open: clr
  Register #(.width(12)) register_8 (.D(D), .en(decoder_1_out7), .Q(register_8_q), .clk(CLK));  // open: clr
  Multiplexer #(.select(4), .width(12)) multiplexer_2 (
    .in0(register_1_q), .in1(register_2_q), .in2(register_3_q), .in3(register_4_q), .in4(register_5_q),
    .in5(register_6_q), .in6(register_7_q), .in7(register_8_q), .in8(register_9_q), .in9(register_10_q),
    .in10(register_11_q), .in11(register_12_q), .in12(register_13_q), .in13(register_14_q),
    .in14(register_16_q), .in15(IP), .out(OP_B), .sel(SEL_B), .en(EN_B));
  Register #(.width(12)) register_9 (.D(D), .en(decoder_1_out8), .Q(register_9_q), .clk(CLK));  // open: clr
  Register #(.width(12)) register_10 (.D(D), .en(decoder_1_out9), .Q(register_10_q), .clk(CLK));  // open: clr
  Register #(.width(12)) register_11 (.D(D), .en(decoder_1_out10), .Q(register_11_q), .clk(CLK));  // open: clr
  Register #(.width(12)) register_12 (.D(D), .en(decoder_1_out11), .Q(register_12_q), .clk(CLK));  // open: clr
  Register #(.width(12)) register_13 (.D(D), .en(decoder_1_out12), .Q(register_13_q), .clk(CLK));  // open: clr
  Register #(.width(12)) register_14 (.D(D), .en(decoder_1_out13), .Q(register_14_q), .clk(CLK));  // open: clr
  Pull_Resistor pull_resistor_1 (.node(pull_resistor_1_node));
  Transistor transistor_1 (.in(IP_INC), .out(pull_resistor_1_node), .gate(decoder_1_out15));
  Multiplexer #(.width(12), .enable("false")) multiplexer_3 (
    .in0(D), .in1(adder_1_out), .out(multiplexer_3_out), .sel(pull_resistor_1_node));
  Register #(.width(12)) register_15 (.D(multiplexer_3_out), .en(or_2_out), .Q(IP), .clk(CLK));  // open: clr
  or or_1 (or_1_out, decoder_1_out14, decoder_1_out15);
  or or_2 (or_2_out, decoder_1_out15, IP_INC);
  Multiplexer #(.width(12), .enable("false")) multiplexer_4 (
    .in0(D), .in1(IP), .out(multiplexer_4_out), .sel(decoder_1_out15));
  Register #(.width(12)) register_16 (.D(multiplexer_4_out), .en(or_1_out), .Q(register_16_q), .clk(CLK));  // open: clr
  Adder #(.width(12)) adder_1 (.a(IP), .b(12'h1), .out(adder_1_out));  // open: cin, cout
endmodule

// PS1
module PipeSt1 (
  input  [11:0] A,
  input  IR_VALID,
  input  CLK,
  input  PS2_ACK,
  input  [11:0] IMMWD,
  input  [4:0] OPCODE,
  input  [3:0] DSTREG,
  input  [3:0] SRCREG,
  input  [1:0] SRCMODE,
  output [3:0] SEL_A,
  output EN_A,
  output [11:0] OUT_DATA,
  output [4:0] OUT_OPCODE,
  output [3:0] OUT_DSTREG,
  output OUT_READY,
  output INS_STROBE
);

  wire d_ff_2_q, d_ff_3_q, decoder_1_out0, not_1_out;
  wire [11:0] multiplexer_1_out;

  D_Flip_Flop d_ff_1 (.clk(CLK), .D(IR_VALID), .Q(INS_STROBE), .en(not_1_out), .reset(d_ff_3_q));  // open: Qn, preset
  not not_1 (not_1_out, INS_STROBE);
  Register #(.width(5)) register_1 (.D(OPCODE), .en(not_1_out), .Q(OUT_OPCODE), .clk(CLK));  // open: clr
  Register #(.width(4)) register_2 (.D(DSTREG), .en(not_1_out), .Q(OUT_DSTREG), .clk(CLK));  // open: clr
  Multiplexer #(.width(12)) multiplexer_1 (
    .in0(A), .in1({12{1'b0}}), .out(multiplexer_1_out), .sel(decoder_1_out0));  // open: en
  Decoder #(.select(2)) decoder_1 (.out0(decoder_1_out0), .out1(EN_A), .sel(SRCMODE));  // open: out2, out3, en
  Adder #(.width(12)) adder_1 (.a(multiplexer_1_out), .b(IMMWD), .out(OUT_DATA));  // open: cin, cout
  D_Flip_Flop d_ff_2 (.clk(PS2_ACK), .D(PS2_ACK), .Q(d_ff_2_q), .reset(not_1_out));  // open: Qn, preset, en
  D_Flip_Flop d_ff_3 (.clk(CLK), .D(d_ff_2_q), .Q(d_ff_3_q));  // open: Qn, preset, en, reset

  assign OUT_READY = INS_STROBE;
  assign SEL_A = SRCREG;
endmodule

// Clk
module clockgen (
  input  CLK,
  output P1,
  output P2,
  output P3
);

  wire decoder_1_out3;
  wire [1:0] counter_1_q;

  Counter #(.width(2), .max('h2)) counter_1 (
    .count(1'b1), .Q(counter_1_q), .clk(CLK), .clr(decoder_1_out3));  // open: load, D, carry
  Decoder #(.select(2), .disabled(0)) decoder_1 (
    .out0(P1), .out1(P2), .out2(P3), .out3(decoder_1_out3), .sel(counter_1_q), .en(CLK));
endmodule

// InstrCtrl
module InstructionControl (
  input  IQRESET,
  input  CLK_P1,
  input  CLK_P2,
  input  CLK_P3,
  input  IR0_CONSUMED,
  input  IR1_CONSUMED,
  input  [11:0] D_IN,
  input  WAIT,
  output IFETCH,
  output IR0_VALID,
  output [11:0] IR0,
  output IR1_VALID,
  output [11:0] IR1
);

  wire IF0_ACTIVE_qn, IR0_VALID_qn, nor_1_out, or_1_out;

  D_Flip_Flop u_IR0_VALID (
    .clk(CLK_P2), .D(1'b1), .Q(IR0_VALID), .Qn(IR0_VALID_qn), .en(nor_1_out), .reset(or_1_out));  // open: preset
  Register #(.width(12)) u_IR0 (.D(D_IN), .en(nor_1_out), .Q(IR0), .clk(CLK_P2));  // open: clr
  and and_1 (IFETCH, CLK_P1, IR0_VALID_qn);
  D_Flip_Flop #(.trigger("falling")) IF0_ACTIVE (
    .clk(CLK_P1), .D(IFETCH), .Qn(IF0_ACTIVE_qn), .reset(CLK_P3));  // open: Q, preset, en
  nor nor_1 (nor_1_out, WAIT, IF0_ACTIVE_qn);
  or or_1 (or_1_out, IR0_CONSUMED, IQRESET);
  D_Flip_Flop u_IR1_VALID (.clk(CLK_P3), .D(1'b1), .Q(IR1_VALID), .reset(IQRESET));  // open: Qn, preset, en
  Register #(.width(12)) u_IR1 (.D(D_IN), .Q(IR1));  // open: en, clk, clr

  // Notes on the sheet:
  //   WAIT: pull=down
endmodule

module InstructionQueue (
  input  CLK_P1,
  input  CLK_P2,
  input  CLK_P3
);
endmodule
