// Logisim project c121b.circ as structural Verilog
module InsnQ (
  input  CLK_PH1,
  input  CLK_PH2,
  input  CLK_PH3,
  input  [11:0] IP,
  input  [3:0] IR0,
  input  INST_ACK,
  input  [3:0] D_IN,
  input  D_WAIT,
  output IFETCH,
  output [11:0] IFETCH_ADDR
);

  wire and_1_out, and_2_out, or_1_out, vhdl_entity_1_p6;

  or or_1 (or_1_out, CLK_PH1, CLK_PH2, CLK_PH3);
  Counter #(.width(4), .max('hf)) QUEUE_STATE (.clk(or_1_out));  // open: clr, load, up, count, D, carry, Q
  // VHDL_Entity #(.content("(*\n--\n-- FIFO entity\n--\n-- From https://electronics.stackexchange.com/a/50189/22169\n-- and assumed to be freely usable\n--\n-- modified to match characteristics of a 74HC40105\n-- i.e. use of 4-bit width and 16 stage depth\n*)\n\nlibrary IEEE;\nuse IEEE.STD_LOGIC_1164.ALL;\nuse IEEE.STD_LOGIC_ARITH.ALL;\nuse IEEE.STD_LOGIC_UNSIGNED.ALL;\n\nentity fifo is\ngeneric (RAMsize: integer := 16);\nport (  data_in: in std_logic_vector (3 downto 0);  \n    clk,nrst: in std_logic;\n    readReq: in std_logic;  \n        writeReq: in std_logic; \n        data_out: out std_logic_vector(3 downto 0); \n        empty: out std_logic;  \n        full: out std_logic;\n    error: out std_logic);\nend fifo;\n\narchitecture Behavioral of fifo is\ntype memory_type is array (0 to RAMsize-1) of std_logic_vector(3 downto 0);\nsignal memory : memory_type :=(others => (others => '0')); \n\nbegin\n  process(clk,nrst)\n  variable read_ptr, write_ptr : std_logic_vector(3 downto 0) := \"0000\";  -- read and write pointers\n  variable isempty , isfull : std_logic :='0';\n  begin\n  if nrst='0' then\n    memory <= (others => (others => '0'));\n    empty <='1';\n    full <='0';\n    data_out <= \"0000\";\n    read_ptr := \"0000\";\n    write_ptr := \"0000\";\n    isempty :='1';\n    isfull :='0';\n    error <='0';\n  elsif clk'event and clk='1' then\n    if readReq='0' and writeReq='0' then\n      error <='0';\n    end if;\n    if readReq='1' then\n      if isempty='1' then\n        error <= '1';\n      else\n        data_out <= memory(conv_integer(read_ptr));\n        isfull :='0';\n        full <='0';\n        error <='0';\n        if read_ptr=conv_std_logic_vector(RAMsize-1,4) then\n          read_ptr := \"0000\";\n        else\n          read_ptr := read_ptr + '1';\n        end if;\n        if read_ptr=write_ptr then\n          isempty:='1';\n          empty <='1';\n        end if;\n      end if;\n    end if;\n    if writeReq='1' then\n      if isfull='1' then\n        error <='1';\n      else\n        memory(conv_integer(write_ptr)) <= data_in;\n        error <='0';\n        isempty :='0';\n        empty <='0';\n        if write_ptr=conv_std_logic_vector(RAMsize-1,4) then\n          write_ptr := \"0000\";\n        else\n          write_ptr := write_ptr + '1';\n        end if;\n        if write_ptr=read_ptr then\n          isfull :='1';\n          full <='1';\n        end if;\n      end if;\n    end if;\n  end if;\n  end process;\n\nend Behavioral;")) vhdl_entity_1: pin names not known; wires that end beside it: D_WAIT, D_IN, or_1_out, INST_ACK, IR0, vhdl_entity_1_p6
  and and_1 (and_1_out, CLK_PH1, ~vhdl_entity_1_p6);  // AND_Gate
  D_Flip_Flop d_ff_1 (.D(and_1_out), .Q(IFETCH));  // open: clk, Qn, preset, reset
  and and_2 (and_2_out, IFETCH, ~INST_ACK);  // AND_Gate
endmodule
