// Digital circuit insnqueue.dig as structural Verilog
// Instruction queue and fetch cycle controller
module insnqueue (
  input  PHI0,
  input  PHI1,
  input  PHI2,
  input  [11:0] D_IN,
  input  WAIT,
  input  IACK,
  input  [11:0] IP,
  output IFETCH,
  output [11:0] IR0,
  output IR0VALID,
  output [3:0] QUEUESTAT,
  output [11:0] A_IFETCH
);

  wire and_1_out, and_2_out, EXPECTING_q, fifo_1_p3, fifo_1_p7, not_1_out, or_1_out;
  wire [11:0] add_1_s;

  and and_1 (and_1_out, ~WAIT, or_1_out, EXPECTING_q);  // And
  or or_1 (or_1_out, PHI2, PHI1, PHI0);
  not not_1 (not_1_out, or_1_out);
  updowncounter updowncounter_1 (.UP(and_1_out), .DOWN(fifo_1_p3), .RESET(1'b0), .CLK(not_1_out), .Q(QUEUESTAT));
  // Fifo #(.Bits(12)) fifo_1: pin names not known; wires that end beside it: D_IN, and_1_out, fifo_1_p3, 1'b0, IR0, IR0VALID, fifo_1_p7
  and and_2 (and_2_out, PHI0, fifo_1_p7);
  Add #(.Bits(12)) add_1 (.a(IP), .b({{8{1'b0}}, QUEUESTAT}), .c_i(1'b0), .s(add_1_s));  // open: c_o
  and and_3 (fifo_1_p3, or_1_out, IACK);
  D_FF d_ff_1 (.D(and_2_out), .C(or_1_out), .Q(IFETCH));  // open: nQ
  Register #(.Bits(12)) register_1 (.D(add_1_s), .C(or_1_out), .en(1'b1), .Q(A_IFETCH));
  D_FF EXPECTING (.D(IFETCH), .C(~or_1_out), .Q(EXPECTING_q));  // open: nQ
endmodule
