// Digital circuit updowncounter.dig as structural Verilog
module updowncounter (
  input  UP,
  input  DOWN,
  input  RESET,
  input  CLK,
  output [3:0] Q
);

  wire not_1_out, xnor_1_out;

  not not_1 (not_1_out, RESET);
  xnor xnor_1 (xnor_1_out, UP, DOWN);
  _74191 _74191_1 (
    .pin1(1'b0), .pin2(Q[1]), .pin3(Q[0]), .pin4(xnor_1_out), .pin5(DOWN), .pin6(Q[2]), .pin7(Q[3]),
    .pin8(1'b0), .pin9(1'b0), .pin10(1'b0), .pin11(not_1_out), .pin14(CLK), .pin15(1'b0), .pin16(1'b1));  // open: pin12, pin13
endmodule

/* Test case Counts up:
           CLK UP DOWN RESET Q      
           0   0  0    0     0      
repeat(15) C   1  0    0     (n+1)  
           C   1  0    0     0      
*/

/* Test case Counts down:
           CLK UP DOWN RESET Q      
           0   0  0    0     0      
repeat(15) C   1  0    0     (n+1)  
repeat(15) C   0  1    0     (14-n)   
*/

/* Test case UP+DOWN does nothing:
           CLK UP DOWN RESET Q      
           0   0  0    0     0      
repeat(7)  C   1  0    0     (n+1)  
           C   1  0    0     8      
           C   1  1    0     8
*/

/* Test case RESET resets to zero:
           CLK UP DOWN RESET Q      
           0   0  0    0     0      
repeat(3)  C   1  0    0     (n+1)  
           C   1  0    0     4
           0   1  0    1     0
repeat(3)  C   1  0    0     (n+1)  
*/

/* Test case Doesn't count while RESET high:
           CLK UP DOWN RESET Q      
           0   0  0    0     0      
repeat(3)  C   1  0    0     (n+1)  
           C   1  0    0     4
           0   1  0    1     0
repeat(3)  C   1  0    1     0
           C   0  1    1     0
*/
