// Digital circuit alu3.dig as structural Verilog
module alu3 (
  input  A_0,
  input  B_0,
  input  C_IN,
  input  A_1,
  input  B_1,
  input  A_2,
  input  B_2,
  input  nX,
  input  N,
  input  nS,
  output Q_0,
  output Q_1,
  output C_OUT,
  output Q_2,
  output C_0,
  output C_1
);

  wire and_1_out, and_2_out, and_3_out, and_4_out, and_5_out, and_6_out, and_7_out, and_8_out, and_9_out,
       and_10_out, and_11_out, and_12_out, and_13_out, or_1_out, or_2_out, or_3_out, xor_1_out, xor_2_out,
       xor_3_out, xor_4_out, xor_5_out, xor_6_out;

  and and_1 (and_1_out, nS, A_0);
  xor xor_1 (xor_1_out, B_0, N);
  and and_2 (and_2_out, nS, A_1);
  xor xor_2 (xor_2_out, N, B_1);
  and and_3 (and_3_out, nS, A_2);
  xor xor_3 (xor_3_out, N, B_2);
  and and_4 (and_4_out, nX, C_IN);
  or or_1 (or_1_out, and_1_out, xor_1_out);
  and and_5 (and_5_out, and_1_out, nX, xor_1_out);
  and and_6 (and_6_out, and_2_out, nX, xor_2_out);
  or or_2 (or_2_out, and_2_out, xor_2_out);
  or or_3 (or_3_out, and_3_out, xor_3_out);
  and and_7 (and_7_out, and_3_out, nX, xor_3_out);
  and and_8 (and_8_out, and_4_out, or_1_out);
  and and_9 (and_9_out, or_2_out, or_1_out, and_4_out);
  and and_10 (and_10_out, and_5_out, or_2_out);
  or or_4 (C_0, and_8_out, and_5_out);
  and and_11 (and_11_out, or_3_out, or_2_out, or_1_out, and_4_out);
  and and_12 (and_12_out, or_3_out, or_2_out, and_5_out);
  and and_13 (and_13_out, or_3_out, and_6_out);
  or or_5 (C_1, and_9_out, and_10_out, and_6_out);
  or or_6 (C_OUT, and_11_out, and_12_out, and_13_out, and_7_out);
  xor xor_4 (xor_4_out, and_1_out, xor_1_out);
  xor xor_5 (xor_5_out, and_2_out, xor_2_out);
  xor xor_6 (xor_6_out, and_3_out, xor_3_out);
  xor xor_7 (Q_0, and_4_out, xor_4_out);
  xor xor_8 (Q_1, C_0, xor_5_out);
  xor xor_9 (Q_2, C_1, xor_6_out);

  // Notes on the sheet:
  //   A_0: pin 4
  //   B_0: pin 7
  //   C_IN: pin 13
  //   Q_0: pin 19
  //   A_1: pin 5
  //   B_1: pin 8
  //   Q_1: pin 18
  //   A_2: pin 6
  //   B_2: pin 9
  //   C_OUT: pin 14
  //   Q_2: pin 17
  //   nX: pin 1, default 1
  //   N: pin 3
  //   nS: pin 2, default 1
  //   C_0: pin 16
  //   C_1: pin 15
  //   P_0
  //   G_0
  //   G_1
  //   P_1
  //   P_2
endmodule

/* Test case Adder (bit 0 only):
C_IN A_0 B_0  Q_0 Q_1
0    0   0    0   0
0    0   1    1   0
0    1   0    1   0
0    1   1    0   1
1    0   0    1   0
1    0   1    0   1
1    1   0    0   1
1    1   1    1   1
*/

/* Test case Adder (bit 0+1):
C_IN A_1 A_0 B_1 B_0  Q_2 Q_1 Q_0 
0     0   0   0   0    0   0   0  
0     1   1   0   1    1   0   0  
0     1   0   1   1    1   0   1  
0     1   1   1   1    1   1   0  
1     1   0   0   1    1   0   0  
*/

/* Test case Adder (bit 0..2):
C_IN  A_2 A_1 A_0  B_2 B_1 B_0  C_OUT Q_2 Q_1 Q_0 
0      0   0   0    0   0   0     0    0   0   0
0      1   1   1    0   0   1     1    0   0   0
0      1   0   1    0   1   0     0    1   1   1
1      1   0   1    0   1   0     1    0   0   0
0      1   1   0    0   1   0     1    0   0   0
*/

/* Test case XOR:
~X A_2 A_1 A_0 B_2 B_1 B_0 Q_2 Q_1 Q_0
 0  0   0   0   0   0   0   0   0   0
 0  1   0   1   0   1   0   1   1   1
 0  1   1   1   1   1   1   0   0   0
 0  0   1   1   1   1   1   1   0   0
*/

/* Test case XOR vs C_IN:
~X C_IN A_0 B_0  Q_0
0    1   0   1    1
0    1   1   1    0
0    1   1   0    1
0    1   0   0    0
*/

/* Test case NXOR:
~X N A_2 A_1 A_0 B_2 B_1 B_0 Q_2 Q_1 Q_0
 0 1  0   0   0   0   0   0   1   1   1
 0 1  1   0   1   0   1   0   0   0   0
 0 1  1   1   1   1   1   1   1   1   1
 0 1  0   1   1   1   1   1   0   1   1
*/

/* Test case Select B / Invert B:
~X ~S N A_2 B_2 A_1 B_1 A_0 B_0   Q_2 Q_1 Q_0
0  0  0  1   0   0   0   1   0     0   0   0
0  0  0  0   1   1   1   0   1     1   1   1
0  0  1  0   1   0   1   1   1     0   0   0
*/
