// Digital circuit alu6.dig as structural Verilog
module alu6 (
  input  [5:0] A,
  input  [5:0] B,
  input  C_IN,
  input  nX,
  input  N,
  input  nS,
  output [5:0] Q,
  output C_OUT
);

  wire alu3_1_c_out;

  alu3 alu3_1 (
    .A_0(A[0]), .B_0(B[0]), .C_IN(C_IN), .A_1(A[1]), .B_1(B[1]), .A_2(A[2]), .B_2(B[2]), .nX(nX), .N(N),
    .nS(nS), .Q_0(Q[0]), .Q_1(Q[1]), .C_OUT(alu3_1_c_out), .Q_2(Q[2]));  // open: C_0, C_1
  alu3 alu3_2 (
    .A_0(A[3]), .B_0(B[3]), .C_IN(alu3_1_c_out), .A_1(A[4]), .B_1(B[4]), .A_2(A[5]), .B_2(B[5]), .nX(nX),
    .N(N), .nS(nS), .Q_0(Q[3]), .Q_1(Q[4]), .C_OUT(C_OUT), .Q_2(Q[5]));  // open: C_0, C_1

  // Notes on the sheet:
  //   nX: default 1
  //   nS: default 1
endmodule

/* Test case Addition:
             C_IN  A   B   C_OUT        Q  
loop(i,500)
  let a = random(64);
  let b = random(64);
               0   (a) (b) ((a+b)>>6)   ((a+b)&63)
               1   (a) (b) ((a+b+1)>>6) ((a+b+1)&63)
end loop
*/

/* Test case Subtraction:
             C_IN N A   B   C_OUT             Q  
loop(i,500)
  let a = random(64);
  let b = random(64);
               1  1 (a) (b) (~((a-b)>>6)&1)   ((a-b)&63)
               0  1 (a) (b) (~((a-b-1)>>6)&1) ((a-b-1)&63)
end loop
*/

/* Test case XOR:
             C_IN ~X A   B   C_OUT  Q  
loop(i,500)
  let a = random(64);
  let b = random(64);
  let c = random(2);
              (c)  0 (a) (b) 0      (a^b)
end loop
*/
