// Digital circuit c61.dig as structural Verilog
module c61 (
  input  clk
);

  wire add_4_c_o, and_1_out, and_2_out, and_5_out, and_6_out, and_7_out, and_8_out, and_10_out, and_11_out,
       and_14_out, and_15_out, and_16_out, and_17_out, and_20_out, and_21_out, carry_incr, comparator_1_eq,
       delay_1_out, delay_2_out, delay_3_out, delay_4_out, ext_s1, extcarry_s1_q, extmode_s1_q, extsel_s1_q,
       invert, isjmp_s1_nq, isjmp_s1_q, isjmp_s2_q, mrsel_s2_q, multiplexer_11_out, nand_1_out, nand_2_out,
       not_1_out, not_2_out, or_1_out, or_2_out, or_3_out, or_5_out, or_7_out, RST_out, valid_s1_nq,
       valid_s1_q, wbe, wbe_0_q, wbe_1_q, wbe_b1, xor_1_out, xor_4_out;
  wire [1:0] addr_last_q_2, and_9_out, extop_s1_q, multiplexer_6_out, multiplexer_17_out, multiplexer_18_out,
       or_4_out;
  wire [1:1] and_12_out;
  wire [2:0] and_18_out, dst_s2_q, flags, INSN_q, insn_s1_q, multiplexer_1_out, multiplexer_5_out,
       multiplexer_7_out, multiplexer_14_out, RA_q, RB_q;
  wire [3:0] addr_last_q, dst_s1_q, multiplexer_19_out;
  wire [3:3] RASET_q;
  wire [5:0] add_1_s, add_2_s, add_4_s, and_13_out, bitextender_1_out, IMM_q, membase_q, multiplexer_2_out,
       multiplexer_3_out, multiplexer_4_out, multiplexer_8_out, multiplexer_9_out, multiplexer_10_out,
       multiplexer_12_out, multiplexer_13_out, multiplexer_15_out, multiplexer_16_out, neg_1_out, or_6_out,
       out_s2_q, ramdualport_1_d, rasrc_s1_q, raval_s1_q, rbim_s1_q, REGS_0_da, REGS_0_db, REGS_1_da,
       REGS_1_db, sub_1_s, xor_2_out, xor_3_out;
  wire [5:4] multiplexer_19_out_2;
  wire [9:0] add_3_s;
  wire [15:0] INSTR_ROM_d;

  Seven_Seg_Hex seven_seg_hex_1 (.d({2'b00, addr_last_q_2}), .dp(1'b0));
  Seven_Seg_Hex seven_seg_hex_2 (.d({2'b00, multiplexer_19_out_2}), .dp(wbe_b1));
  not not_1 (not_1_out, clk);
  Reset #(.invertOutput("false")) RST (.out(RST_out));
  ROM #(.AddrBits(6), .isProgramMemory("true"), .Bits(16)) INSTR_ROM (.A(REGS_0_da), .sel(1'b1), .D(INSTR_ROM_d));
  Seven_Seg_Hex seven_seg_hex_3 (.d(addr_last_q), .dp(clk));
  Seven_Seg_Hex seven_seg_hex_4 (.d(multiplexer_19_out), .dp(and_20_out));
  not not_2 (not_2_out, not_1_out);
  D_FF #(.Bits(3)) INSN (.D(INSTR_ROM_d[15:13]), .C(clk), .Q(INSN_q));  // open: nQ
  D_FF #(.Bits(3)) RA (.D(INSTR_ROM_d[11:9]), .C(clk), .Q(RA_q));  // open: nQ
  D_FF RASET (.D(INSTR_ROM_d[12]), .C(clk), .Q(RASET_q[3]));  // open: nQ
  D_FF #(.Bits(3)) RB (.D(INSTR_ROM_d[8:6]), .C(clk), .Q(RB_q));  // open: nQ
  D_FF #(.Bits(6)) IMM (.D(INSTR_ROM_d[5:0]), .C(clk), .Q(IMM_q));  // open: nQ
  or or_1 (or_1_out, isjmp_s2_q, and_20_out);
  D_FF #(.Bits(6)) addr_last (.D(REGS_0_da), .C(clk), .Q({addr_last_q_2, addr_last_q}));  // open: nQ
  and and_1 (and_1_out, INSN_q[0], INSN_q[1], INSN_q[2]);
  xor xor_1 (xor_1_out, clk, not_2_out);
  Delay #(.delayTime(2)) delay_1 (.in(clk), .out(delay_1_out));
  Multiplexer #(.Bits(3)) multiplexer_1 (.sel(delay_1_out), .in_0(3'b111), .in_1(RA_q), .out(multiplexer_1_out));
  Multiplexer #(.Bits(6)) multiplexer_2 (
    .sel(isjmp_s2_q), .in_0({multiplexer_19_out_2, multiplexer_19_out}), .in_1({addr_last_q_2, addr_last_q}),
    .out(multiplexer_2_out));
  Delay #(.delayTime(2)) delay_2 (.in(clk), .out(delay_2_out));
  Multiplexer #(.Bits(6)) multiplexer_3 (.sel(RST_out), .in_0(add_1_s), .in_1({6{1'b0}}), .out(multiplexer_3_out));
  Multiplexer #(.Bits(6)) multiplexer_4 (
    .sel(delay_2_out), .in_0(multiplexer_3_out), .in_1({multiplexer_19_out_2, multiplexer_19_out}),
    .out(multiplexer_4_out));
  Delay #(.delayTime(2)) delay_3 (.in(clk), .out(delay_3_out));
  Multiplexer #(.Bits(3)) multiplexer_5 (.sel(and_1_out), .in_0(3'b000), .in_1(RB_q), .out(multiplexer_5_out));
  RegisterFile #(.AddrBits(3), .Bits(6)) REGS_0 (
    .Din(multiplexer_4_out), .we(or_2_out), .Rw(multiplexer_7_out), .C(xor_1_out), .Ra(multiplexer_1_out),
    .Rb(RB_q), .Da(REGS_0_da), .Db(REGS_0_db));
  RegisterFile #(.AddrBits(3), .Bits(6)) REGS_1 (
    .Din(multiplexer_2_out), .we(or_1_out), .Rw(dst_s2_q), .C(xor_1_out), .Ra(RA_q), .Rb(multiplexer_5_out),
    .Da(REGS_1_da), .Db(REGS_1_db));
  Multiplexer #(.Bits(2)) multiplexer_6 (.sel(and_1_out), .in_0(2'b01), .in_1(IMM_q[1:0]), .out(multiplexer_6_out));
  Multiplexer #(.Bits(3)) multiplexer_7 (.sel(delay_3_out), .in_0(3'b111), .in_1(dst_s2_q), .out(multiplexer_7_out));
  or or_2 (or_2_out, ~delay_3_out, wbe_b1);  // Or
  Add #(.Bits(6)) add_1 (.a(REGS_0_da), .b(6'b000001), .c_i(1'b0), .s(add_1_s));  // open: c_o
  Multiplexer #(.Bits(6)) multiplexer_8 (.sel(RASET_q[3]), .in_0(REGS_0_da), .in_1(REGS_1_da), .out(multiplexer_8_out));
  Comparator #(.Bits(4)) comparator_1 (.a({RASET_q[3], RA_q}), .b(4'b0111), .eq(comparator_1_eq));  // open: gt, lt
  Add #(.Bits(6)) add_2 (.a(REGS_0_db), .b(IMM_q), .c_i(1'b0), .s(add_2_s), .c_o(carry_incr));
  Delay #(.delayTime(2)) delay_4 (.in(delay_3_out), .out(delay_4_out));
  D_FF isjmp_s2 (.D(and_2_out), .C(delay_4_out), .Q(isjmp_s2_q));  // open: nQ
  and and_2 (and_2_out, isjmp_s1_q, wbe_b1);
  Multiplexer #(.Bits(6)) multiplexer_9 (.sel(and_1_out), .in_0(add_2_s), .in_1(IMM_q), .out(multiplexer_9_out));
  Multiplexer #(.Selector_Bits(2), .Bits(6)) multiplexer_10 (
    .sel(multiplexer_6_out), .in_0(multiplexer_8_out), .in_1(add_1_s), .in_2(REGS_1_db),
    .in_3({1'b0, multiplexer_8_out[5:1]}), .out(multiplexer_10_out));
  Multiplexer #(.Selector_Bits(2)) multiplexer_11 (
    .sel(multiplexer_6_out), .in_0(1'b0), .in_1(carry_incr), .in_2(1'b0), .in_3(multiplexer_8_out[0]),
    .out(multiplexer_11_out));
  D_FF valid_s1 (.D(or_3_out), .C(not_1_out), .Q(valid_s1_q), .nQ(valid_s1_nq));
  D_FF #(.Bits(4)) dst_s1 (.D({RASET_q[3], RA_q}), .C(not_1_out), .Q(dst_s1_q));  // open: nQ
  D_FF isjmp_s1 (.D(comparator_1_eq), .C(not_1_out), .Q(isjmp_s1_q), .nQ(isjmp_s1_nq));
  D_FF #(.Bits(6)) rbim_s1 (.D(multiplexer_9_out), .C(not_1_out), .Q(rbim_s1_q));  // open: nQ
  D_FF #(.Bits(6)) rasrc_s1 (.D(multiplexer_10_out), .C(not_1_out), .Q(rasrc_s1_q));  // open: nQ
  D_FF #(.Bits(6)) membase (.D(REGS_1_db), .C(not_1_out), .Q(membase_q));  // open: nQ
  D_FF #(.Bits(6)) raval_s1 (.D(multiplexer_8_out), .C(not_1_out), .Q(raval_s1_q));  // open: nQ
  D_FF #(.Bits(3)) insn_s1 (.D(INSN_q), .C(not_1_out), .Q(insn_s1_q));  // open: nQ
  D_FF u_ext_s1 (.D(and_1_out), .C(not_1_out), .Q(ext_s1));  // open: nQ
  D_FF extmode_s1 (.D(IMM_q[5]), .C(not_1_out), .Q(extmode_s1_q));  // open: nQ
  D_FF extsel_s1 (.D(IMM_q[4]), .C(not_1_out), .Q(extsel_s1_q));  // open: nQ
  D_FF #(.Bits(2)) extop_s1 (.D(IMM_q[3:2]), .C(not_1_out), .Q(extop_s1_q));  // open: nQ
  D_FF extcarry_s1 (.D(multiplexer_11_out), .C(not_1_out), .Q(extcarry_s1_q));  // open: nQ
  LED led_1 (.in(flags[0]));
  LED led_2 (.in(flags[1]));
  or or_3 (or_3_out, valid_s1_nq, and_16_out);
  and and_3 (wbe, valid_s1_q, nand_1_out);
  LED led_3 (.in(valid_s1_q));
  Neg #(.Bits(6)) neg_1 (.in(rbim_s1_q), .out(neg_1_out));
  Multiplexer #(.Bits(6)) multiplexer_12 (
    .sel(insn_s1_q[0]), .in_0(rbim_s1_q), .in_1(raval_s1_q), .out(multiplexer_12_out));
  and and_4 (invert, ext_s1, extmode_s1_q, extsel_s1_q);
  and and_5 (and_5_out, insn_s1_q[2], ~insn_s1_q[1], add_3_s[9]);  // And
  LED led_4 (.in(flags[2]));
  Add #(.Bits(10)) add_3 (
    .a({4'b0000, multiplexer_12_out}), .b({membase_q, 4'b0000}), .c_i(1'b0), .s(add_3_s));  // open: c_o
  and and_6 (and_6_out, wbe, ~dst_s1_q[3]);  // And
  and and_7 (and_7_out, dst_s1_q[3], wbe);
  Multiplexer #(.Bits(6)) multiplexer_13 (
    .sel(and_8_out), .in_0(rbim_s1_q), .in_1(neg_1_out), .out(multiplexer_13_out));
  and and_8 (and_8_out, ~insn_s1_q[0], insn_s1_q[1]);  // And
  and and_9 (and_9_out[1], insn_s1_q[0], insn_s1_q[1], ~insn_s1_q[2]);  // And
  nor nor_1 (and_9_out[0], insn_s1_q[0], insn_s1_q[1], insn_s1_q[2]);
  and and_10 (and_10_out, ext_s1, ~extmode_s1_q, ~extsel_s1_q);  // And
  and and_11 (and_11_out, ext_s1, ~extmode_s1_q, extsel_s1_q);  // And
  and and_12 (and_12_out[1], ~add_3_s[9], ~insn_s1_q[1], insn_s1_q[2]);  // And
  Add #(.Bits(6)) add_4 (.a(multiplexer_13_out), .b(raval_s1_q), .c_i(1'b0), .s(add_4_s), .c_o(add_4_c_o));
  assign xor_2_out = rbim_s1_q ^ raval_s1_q;  // XOr xor_2, 6 bits wide
  nand nand_1 (nand_1_out, and_8_out, ~insn_s1_q[2]);  // NAnd
  Multiplexer multiplexer_14 (.sel(ext_s1), .in_0(add_4_c_o), .in_1(extcarry_s1_q), .out(multiplexer_14_out[0]));
  assign and_13_out = raval_s1_q & multiplexer_15_out;  // And and_13, 6 bits wide
  Multiplexer #(.Selector_Bits(2), .Bits(6)) multiplexer_15 (
    .sel(or_4_out), .in_0(add_4_s), .in_1(rbim_s1_q), .in_2(xor_2_out), .in_3(rasrc_s1_q),
    .out(multiplexer_15_out));
  assign or_4_out = and_9_out | multiplexer_17_out | {2{and_12_out[1]}};  // Or or_4, 2 bits wide
  and and_14 (and_14_out, insn_s1_q[0], and_12_out[1]);
  and and_15 (and_15_out, and_12_out[1], ~insn_s1_q[0]);  // And
  and and_16 (and_16_out, isjmp_s1_nq, nand_2_out, or_5_out);
  Multiplexer #(.Bits(6), .Selector_Bits(2)) multiplexer_16 (
    .sel(multiplexer_18_out), .in_0(multiplexer_15_out), .in_1(and_13_out), .in_2(or_6_out), .in_3(sub_1_s),
    .out(multiplexer_16_out));
  Multiplexer #(.Bits(2)) multiplexer_17 (.sel(and_10_out), .in_0({2{ext_s1}}), .in_1(2'b01), .out(multiplexer_17_out));
  and and_17 (and_17_out, ext_s1, ~and_10_out);  // And
  or or_5 (or_5_out, multiplexer_14_out[1], nand_1_out);
  D_FF #(.Bits(3)) u_flags (.D(multiplexer_14_out), .C(and_21_out), .Q(flags));  // open: nQ
  assign or_6_out = raval_s1_q | multiplexer_15_out;  // Or or_6, 6 bits wide
  BitExtender #(.inputBits(1), .outputBits(6)) bitextender_1 (.in(invert), .out(bitextender_1_out));
  Multiplexer #(.Bits(2)) multiplexer_18 (.sel(and_17_out), .in_0(2'b00), .in_1(extop_s1_q), .out(multiplexer_18_out));
  assign xor_3_out = bitextender_1_out ^ multiplexer_16_out;  // XOr xor_3, 6 bits wide
  nand nand_2 (nand_2_out, and_11_out, xor_4_out);
  xor xor_4 (xor_4_out, extop_s1_q[1], or_7_out);
  or or_7 (or_7_out, and_18_out[0], and_18_out[1], and_18_out[2]);
  assign and_18_out = flags & rbim_s1_q[2:0];  // And and_18, 3 bits wide
  Sub #(.Bits(6)) sub_1 (.a(raval_s1_q), .b(multiplexer_15_out), .c_i(1'b0), .s(sub_1_s));  // open: c_o
  Comparator #(.Signed("true"), .Bits(6)) comparator_2 (
    .a(xor_3_out), .b({6{1'b0}}), .eq(multiplexer_14_out[1]), .lt(multiplexer_14_out[2]));  // open: gt
  D_FF mrsel_s2 (.D(and_15_out), .C(and_21_out), .Q(mrsel_s2_q));  // open: nQ
  D_FF wbe_0 (.D(and_6_out), .C(delay_3_out), .Q(wbe_0_q));  // open: nQ
  D_FF #(.Bits(3)) dst_s2 (.D(dst_s1_q[2:0]), .C(delay_3_out), .Q(dst_s2_q));  // open: nQ
  D_FF wbe_1 (.D(and_7_out), .C(delay_3_out), .Q(wbe_1_q));  // open: nQ
  D_FF #(.Bits(6)) out_s2 (.D(xor_3_out), .C(delay_3_out), .Q(out_s2_q));  // open: nQ
  RAMDualPort #(.AddrBits(9), .Bits(6)) ramdualport_1 (
    .A(add_3_s[8:0]), .Din(rbim_s1_q), .str(and_14_out), .C(and_21_out), .ld(and_15_out), .D(ramdualport_1_d));
  and and_19 (wbe_b1, wbe_0_q, delay_3_out);
  and and_20 (and_20_out, wbe_1_q, delay_3_out);
  and and_21 (and_21_out, wbe, ~and_11_out, delay_3_out);  // And
  Multiplexer #(.Bits(6)) multiplexer_19 (
    .sel(mrsel_s2_q), .in_0(out_s2_q), .in_1(ramdualport_1_d),
    .out({multiplexer_19_out_2, multiplexer_19_out}));

  // Notes on the sheet:
  //   contents of INSTR_ROM (hex, n*v repeats v):
  //   e00f,e207,e021,f203,f401,e06a,e2b6,f201,e2ba,e066,e231,e06e
  //   CLK_TRANS
  //   ISJMP_S2
  //   R_B2
  //   WBE_B2J
  //   WBE_B2
  //   R_B1
  //   RA_COMB
  //   OP_EXT
  //   RESULT
  //   ADDR_NEXT
  //   ADDR_INS
  //   WSEL_B1
  //   SRC_SEL
  //   WBE_B1
  //   RB+IMM
  //   IMM
  //   .RA
  //   .RA_B0+1
  //   .RB_B2
  //   .RA>>1
  //   OP_IO
  //   A_DATA
  //   ~MEM/IO
  //   OP_SUBCMP
  //   ~WRITEBACKSUPPRESS
  //   F_ZERO
  //   OP_XOR
  //   OP_MOV
  //   OP_LDC
  //   OP_IFxxx
  //   OP_MEM
  //   ~OP_IFEQ
  //   ~SKIPNEXT
  //   OP_STORE
  //   OP_LOAD
  //   RES_ALU
endmodule
