// Digital circuit i81.dig as structural Verilog
module i81 (
  input  CLK,
  input  [23:0] ADDR_IN,
  input  [15:0] D_IN,
  input  nBUSACK,
  input  nDEVSEL,
  input  nRD_IN,
  input  nWR_IN,
  input  nBUSIDLE,
  input  [7:0] DQFULL_A,
  input  [7:0] DQFULL_B,
  output nBUSRQ,
  output [23:0] ADDR_OUT,
  output [15:0] D_OUT,
  output nRD_OUT,
  output nWR_OUT,
  output nINTR,
  output nDQWRITE_A,
  output [7:0] D_DQ_A,
  output [2:0] DQSEL_A,
  output nDQWRITE_B,
  output [7:0] D_DQ_B,
  output [2:0] DQSEL_B
);

  dmac dmac_1 (
    .CLK(CLK), .ADDR_IN(ADDR_IN), .D_IN(D_IN), .nDEVSEL(nDEVSEL), .nRD_IN(nRD_IN), .nWR_IN(nWR_IN),
    .nBUSACK(nBUSACK), .nBUSIDLE(nBUSIDLE), .ADDR_OUT(ADDR_OUT), .D_OUT(D_OUT), .nRD_OUT(nRD_OUT),
    .nWR_OUT(nWR_OUT), .nBUSRQ(nBUSRQ));  // open: QSEL_RQ, BSEL_RQ, ADDR_RQ, PRIO_RQ, D_QOUT, QSEL_OUT, BSEL_OUT, nWR_Q
endmodule
