// Digital circuit queuehandler.dig as structural Verilog
module queuehandler (
  input  CLK,
  input  [7:0] D_QIN,
  input  [3:0] QSEL_IN,
  input  [1:0] BSEL_IN,
  input  nWR_Q,
  input  [3:0] QSEL_RQCH,
  input  [1:0] BSEL_RQCH,
  input  [23:0] ADDR_RQCH,
  input  PRIO_RQCH,
  input  ACK_QIN_2,
  output [7:0] D_QINCH,
  output [3:0] QSEL_INCH,
  output [1:0] BSEL_INCH,
  output nWR_QCH,
  output [3:0] QSEL_RQ,
  output [2:0] BSEL_RQ,
  output [23:0] ADDR_RQ,
  output PRIO_RQ,
  output ACK_QIN
);

  wire and_1_out, INSNREADY, nACK_QIN, OPCODELOADED, ucdecode_1_p3;
  wire [0:0] undriven_2;
  wire [2:0] multiplexer_1_out, multiplexer_2_out, UCSTEP_q;
  wire [2:1] undriven;
  wire [2:2] STATUS_q;
  wire [3:0] OPERAND_BN_q;
  wire [4:0] OPCODE_C_q, OPCODE_N_q;
  wire [7:0] OPERAND_AN_q;

  or or_1 (nACK_QIN, BSEL_IN[0], nWR_Q, OPCODELOADED);
  and and_1 (and_1_out, nACK_QIN, ~ucdecode_1_p3);  // And
  Multiplexer multiplexer_1 (.sel(ucdecode_1_p3), .in_0(1'b1), .in_1(1'b0), .out(multiplexer_1_out[0]));
  Register #(.Bits(3)) STATUS (
    .D(multiplexer_1_out), .C(CLK), .en(~and_1_out), .Q({STATUS_q[2], INSNREADY, OPCODELOADED}));
  Register #(.Bits(5)) OPCODE_N (.D(5'b10000), .C(CLK), .en(~nACK_QIN), .Q(OPCODE_N_q));
  Register #(.Bits(8)) OPERAND_AN (.D(D_QIN), .C(CLK), .en(~nACK_QIN), .Q(OPERAND_AN_q));
  Register #(.Bits(4)) OPERAND_BN (.D(QSEL_IN), .C(CLK), .en(~nACK_QIN), .Q(OPERAND_BN_q));
  RAMSinglePort #(.AddrBits(15), .Bits(8)) _61256_70_or_similar ();  // open: A, str, C, ld, D
  Multiplexer #(.Bits(3)) multiplexer_2 (
    .sel(ucdecode_1_p3), .in_1({undriven, 1'b0}), .out(multiplexer_2_out));  // open: in_0
  Register #(.Bits(3)) UCSTEP (.D(multiplexer_2_out), .C(CLK), .en(ucdecode_1_p3), .Q(UCSTEP_q));
  Register #(.Bits(5)) OPCODE_C (.D(OPCODE_N_q), .C(CLK), .en(ucdecode_1_p3), .Q(OPCODE_C_q));
  Register #(.Bits(8)) OPERAND_AC (.D(OPERAND_AN_q), .C(CLK), .en(ucdecode_1_p3));  // open: Q
  Register #(.Bits(4)) OPERAND_BC (.D(OPERAND_BN_q), .C(CLK), .en(ucdecode_1_p3));  // open: Q
  // ucdecode ucdecode_1: pin names not known; wires that end beside it: UCSTEP_q, OPCODE_C_q, ucdecode_1_p3
  assign QSEL_RQ[0] = undriven_2[0] ? QSEL_RQCH[0] : 1'bz;  // Driver driver_1
  assign BSEL_RQ[0] = undriven_2[0] ? undriven_2[0] : 1'bz;  // Driver driver_2
  assign ADDR_RQ[0] = undriven_2[0] ? ADDR_RQCH[0] : 1'bz;  // Driver driver_3
  assign PRIO_RQ = undriven_2[0] ? PRIO_RQCH : 1'bz;  // Driver driver_4
  or or_2 (ACK_QIN, ~nACK_QIN, ACK_QIN_2);  // Or
  // Pins of 1 and 4 bits meet at QSEL_RQCH
  // Pins of 1 and 24 bits meet at ADDR_RQCH
  // Pins of 1 and 4 bits meet at QSEL_RQ
  // Pins of 1 and 3 bits meet at BSEL_RQ
  // Pins of 1 and 24 bits meet at ADDR_RQ
  // Pins of 1 and 2 bits meet at {BSEL_RQCH[0], undriven_2[0]}
  // Pins of 1 and 3 bits meet at multiplexer_1_out
  // Pins of 1 and 3 bits meet at {undriven, 1'b0}
  // Pins of 1 and 3 bits meet at 3'b011
  // Pins of 1 and 3 bits meet at 3'b000

  assign BSEL_INCH = {1'b1, BSEL_IN[1]};
  assign D_QINCH = D_QIN;
  assign nWR_QCH = nWR_Q;
  assign QSEL_INCH = QSEL_IN;

  // Notes on the sheet:
  //   Connections from
  //   chained modules
  //   Connections from
  //   DMA controller
  //   ~DMARQ
  //   ~ENABLE
  //   DMARQCHAIN
  //   Internal opcode: QSTORE
  //   Channel Queue Memory
  //   NEXTINSN
  //   Connections to
  //   chained modules
  //   Connections to
  //   DMA controller
endmodule
