// Digital circuit ucdecode.dig as structural Verilog
module ucdecode (
  input  [2:0] UCSTEP,
  input  [4:0] OPCODE,
  output NEXTINSN,
  output UCS_1,
  output UCS_2
);

  and and_1 (NEXTINSN, UCSTEP[2], UCSTEP[1], UCSTEP[0], OPCODE[4], OPCODE[3], OPCODE[2], OPCODE[1], OPCODE[0]);

  // Notes on the sheet:
  //   OPCODE MAP
  //   YIELD A
  //   YIELD B
  //   TAKE A
  //   TAKE B
  //   FETCH A, #0
  //   SEND A, #n
  //   LOAD A, (nn)
  //   LOAD A, (B)
  //   EX A, B
  //   LDC A, n
  //   STORE (nn), A
  //   STORE (B), A
  //   OP n, A, B
  //   MARK
  //   RESET NZ
  //   (prefix for extended ops)
  //   74181 OPCODE MAPPING
  //   00000 F=A+C
  //   00001 F=(A|B)+C    ?
  //   00011 F=-1+C
  //   00110 F=A-B-1+C
  //   01001 F=A+B+C
  //   01011 F=(A&B)-1+C
  //   01100 F=A+A+C
  //   01111 F=A-1+C
  //   0
  //   1
  //   2
  //   3
  //   4
  //   5
  //   6
  //   7
  //   0
  //   PASS nn, @m
  //   SWITCH @n
  //   IGNORE
  //   STOP
  //   FETCH B, #n
  //   SEND B, #n
  //   IN A, (nn)
  //   IN B, (nn)
  //   CP A,B
  //   LDC B, n
  //   OUT (nn), A
  //   OUT (nn), B
  //   OP m, A, nn
  //   SKIP NZ
  //   RESET Z
  //   SKIP Z
  //   10000 F=not A
  //   10001 F=not (A|B)
  //   10011 F=0
  //   10110 F=AXB
  //   11001 F=not AXB
  //   11011 F=A&B
  //   11100 F=1
  //   11110 F=A|B
  //   8
  //   QUEUE MEMORY MAP
  //   Each queue has 2KB allocated.  Address fields:
  //     0bQQQQXXXNNNNNNNN (15 bits = 32K)
  //   Q: queue number. 16 queues exist; these can be arbitrarily assigned to
  //   8 DMA channels (which may be set up for either read or write),
  //   8 IO input channels  and 8 IO output channels.  Each queue can have
  //   one input and one output.
  //   X: memory block - 8 memory blocks may be assigned to different functions
  //   by control register settings:
  //   * queue storage
  //   * queue filler program (may not be assigned to block 0)
  //   * output interrupt handling program (may not be assigned to block 0)
  //   * scratch storage (may only be in blocks 0-3)
  //   * callable peripheral control functions
  //   * translation table
  //   (input interrupts may also exist, but will simply cause execution of queue filler
  //   to be started for a single run)
  //   N: offset within block, determined by usage.
  //   Queue registers (bit numbers):
  //   0-2: queue storage block
  //   3-5: filler program block
  //   6-7: scratch block
  //   8-10: output interrupt handler block
  //   11: 1 if currently handling an interrupt
  //   12-19: program counter
  //   20: 0 => 'A' register stored in 'X', 'B' register stored in 'Y'; 1 => converse
  //   21: zero flag for last operation
  //   22: carry flag for last operation
  //   23: last queue operation was 0=take; 1=put
  //   24-31: 'X' register
  //   32-39: 'Y' register
  //   40-43: 'P' register
  //   44-47: 'S' register
  //   48-55: queue head pointer
  //   56-63: queue tail pointer
  //   DMA Registers:
  //   00-23: current DMA pointer
  //   24-39: DMA length remaining
  //   40-47: DMA stride
  //   48-51: Target queue ID
  //   52: rd/~wr
  //   53: Priority
  //   54: Active
  //   UCS_2.._1 selects next ucode step:
  //     00 - hold
  //     01 - increment
  //     10 - set to 1
  //     11 - set to 5
endmodule
